# Fritzing sketch schema (saved by Fritzing 1.0.5)

parts:
  Mod1 = Amica NodeMCU DEVKIT 1.0
  SEN1 = Pulse Sensor [package=SIP-3]  # not connected
  Mod2 = Amica NodeMCU DEVKIT 1.0  # not connected
  Part1 = MyoWare Power Shield

nets:
  N1: Mod1.pin1, Mod1.pin_10, Part1.VCC
  N2: Mod1.pin2, Mod1.pin_9, Part1.GND
  N3: Mod1.pin_16, Part1.SIG

notes:
  garmin watch

custom parts:
  Pulse Sensor: Pulse Sensor Optical Heart Beat Sensor
